// Digital circuit 8位寄存器.dig as structural Verilog
module \_8位寄存器  (
  input  [7:0] Din,
  input  clock,
  input  We,
  input  Oe,
  output [7:0] Dout,
  output [7:0] stored_data
);

  Register #(.Bits(8)) register_1 (.D(Din), .C(clock), .en(We), .Q(stored_data));
  assign Dout = Oe ? stored_data : 8'bz;  // Driver driver_1
endmodule
