// Digital circuit CPU.dig as structural Verilog
module CPU (
  input  WE,
  input  OE,
  input  WE_2,
  input  OE_2,
  input  WE_3,
  input  OE_3,
  input  OE_4,
  input  OE_5,
  input  [7:0] \测试数据 ,
  input  WE_4,
  input  OE_6,
  input  WE_5,
  input  OE_7,
  input  WE_6,
  input  OE_8,
  input  WE_7,
  input  OE_9,
  input  WE_8,
  input  OE_10,
  input  OE_11,
  input  WE_9,
  input  OE_12,
  output [7:0] ALU_Result,
  output Carry,
  output [7:0] OutputReg,
  output [7:0] RegA,
  output [7:0] RegB,
  output [7:0] IR,
  output [7:0] MBR,
  output [3:0] MAR,
  output [3:0] PC
);

  wire clock;
  wire [3:0] \_4位寄存器_1_dout , \_8位寄存器_1_dout , \_8位寄存器_1_dout_2 ;
  wire [7:0] \_8位寄存器_2_dout , \_8位寄存器_3_dout , \_8位寄存器_4_dout , \_8位数加法器_可控制输出_1_dout ;

  Button button_1 (.out(clock));
  Counter #(.Bits(2), .isProgramCounter("true")) counter_1 (
    .en(WE_8), .C(clock), .clr(OE_10), .out(PC[1:0]));  // open: ovf
  \_8位寄存器  \_8位寄存器_1  (
    .Din(\_8位寄存器_4_dout ), .clock(clock), .We(WE_4), .Oe(OE_6), .Dout({\_8位寄存器_1_dout_2 , \_8位寄存器_1_dout }),
    .stored_data(IR));
  \_8位寄存器  \_8位寄存器_2  (
    .Din(\_8位寄存器_4_dout ), .clock(clock), .We(WE), .Oe(OE), .Dout(\_8位寄存器_2_dout ), .stored_data(RegA));
  \_8位寄存器  \_8位寄存器_3  (
    .Din(\_8位寄存器_4_dout ), .clock(clock), .We(WE_2), .Oe(OE_2), .Dout(\_8位寄存器_3_dout ), .stored_data(RegB));
  assign \_8位寄存器_1_dout_2  = OE_11 ? {2'b00, PC[1:0]} : 4'bz;  // Driver driver_1
  \_8位数加法器_可控制输出  \_8位数加法器_可控制输出_1  (
    .RegA(\_8位寄存器_2_dout ), .RegB(\_8位寄存器_3_dout ), .Oe(OE_4), .Dout(\_8位数加法器_可控制输出_1_dout ),
    .ALU_Result(ALU_Result), .Carry(Carry));
  \_8位寄存器  \_8位寄存器_4  (
    .Din(\_8位数加法器_可控制输出_1_dout ), .clock(clock), .We(WE_3), .Oe(OE_3), .Dout(\_8位寄存器_4_dout ),
    .stored_data(OutputReg));
  \_4位寄存器  \_4位寄存器_1  (
    .Din(\_8位寄存器_1_dout_2 ), .clock(clock), .We(WE_5), .Oe(OE_7), .Dout(\_4位寄存器_1_dout ), .stored_data(MAR));
  assign \_8位寄存器_4_dout  = OE_5 ? \测试数据  : 8'bz;  // Driver driver_2
  \_8位寄存器  \MBR内部缓存寄存器  (
    .Din(\_8位寄存器_4_dout ), .clock(clock), .We(WE_6), .Oe(OE_8), .Dout(\_8位寄存器_4_dout ), .stored_data(MBR));
  \_8位寄存器  \u_输出寄存器  (
    .Din(\_8位寄存器_4_dout ), .clock(clock), .We(WE_9), .Oe(OE_12), .Dout(\_8位寄存器_4_dout ));  // open: stored_data
  EEPROMDualPort #(.AddrBits(4), .Bits(8)) eepromdualport_1 (
    .A(\_4位寄存器_1_dout ), .Din(\_8位寄存器_4_dout ), .str(WE_7), .C(clock), .ld(OE_9), .D(\_8位寄存器_4_dout ));

  assign PC[3:2] = 2'b00;

  // Notes on the sheet:
  //   ALU_Result: stored data
  //   Carry: stored data
  //   OutputReg: stored data
  //   MBR: stored data
  //   2位计数器要连4位计数器，所以要用分裂器
  //   IR CPU指令寄存器
  //   RegA
  //   RegB
  //   CPU内部地址总线
  //   MAR 内存地址寄存器
  //   Output Reg
  //   CPU外部地址总线
  //   内部公共数据总线
  //   contents of eepromdualport_1 (hex, n*v repeats v):
  //   0,1,2,3,4,5,6,7,8,9,a,b,c,d,e,f
  //   外部数据总线
endmodule
