// Digital circuit Latch.dig as structural Verilog
module Latch (
  input  Din,
  input  WE,
  output Out
);

  wire \与门制作_1_c , \与门制作_2_c , \或门制作_1_c , \非门_1_c , \非门_2_c ;

  \非门  \u_非门_1  (.A(Din), .C(\非门_1_c ));
  \与门制作  \u_与门制作_1  (.A(Din), .B(WE), .C(\与门制作_1_c ));
  \与门制作  \u_与门制作_2  (.A(\非门_1_c ), .B(WE), .C(\与门制作_2_c ));
  \或门制作  \u_或门制作_1  (.B(Out), .A(\与门制作_1_c ), .C(\或门制作_1_c ));
  \非门  \u_非门_2  (.A(\与门制作_2_c ), .C(\非门_2_c ));
  \与门制作  \u_与门制作_3  (.A(\或门制作_1_c ), .B(\非门_2_c ), .C(Out));

  // Notes on the sheet:
  //   Din: 数据输入
  //   数据输入
  //   可否写入
  //   锁存器（10个继电器）
endmodule
