// Digital circuit 内存EPRM示例.dig as structural Verilog
module \内存EPRM示例  (
  input  [3:0] Addr,
  input  [7:0] Din,
  input  WE,
  input  OE,
  output [7:0] DOut
);

  wire Clock_out;

  Button Clock (.out(Clock_out));
  EEPROMDualPort #(.AddrBits(4), .Bits(8)) eepromdualport_1 (
    .A(Addr), .Din(Din), .str(WE), .C(Clock_out), .ld(OE), .D(DOut));

  // Notes on the sheet:
  //   断点之后数据还在，就是读取数据慢一点
  //   contents of eepromdualport_1 (hex, n*v repeats v):
  //   0,1,2,3,4,5,6,7,8,9,a,b,c,d,e,f
endmodule
