// Digital circuit 寄存器输入输出案例.dig as structural Verilog
module \寄存器输入输出案例  (
  input  [7:0] Din,
  input  We,
  input  clk,
  output [7:0] out_3
);

  Register #(.Bits(8)) register_1 (.D(Din), .C(clk), .en(We), .Q(out_3));
endmodule
