// Digital circuit 异或门制作2.dig as structural Verilog
module \异或门制作2  (
  input  A,
  input  B,
  output C
);

  wire nand_1_out, or_1_out;

  nand nand_1 (nand_1_out, A, B);
  or or_1 (or_1_out, A, B);
  and and_1 (C, nand_1_out, or_1_out);
endmodule
