// Digital circuit 或门制作.dig as structural Verilog
module \或门制作  (
  input  B,
  input  A,
  output C
);

  // RelayDT relaydt_1: pin names not known; wires that end beside it: A, 1'b1, B, 1'b0, C, 1'b0
  // RelayDT relaydt_2: pin names not known; wires that end beside it: 1'b1, C
  PullDown pulldown_1 (.out(C));
endmodule
