// Digital circuit 边缘触发锁存器.dig as structural Verilog
module \边缘触发锁存器  (
  input  WE,
  input  [7:0] Din,
  output [7:0] Out
);

  \锁存器  \u_锁存器_1  (.Din(Din[0]), .We(WE), .Out(Out[0]));
  \锁存器  \u_锁存器_2  (.Din(Din[1]), .We(WE), .Out(Out[1]));
  \锁存器  \u_锁存器_3  (.Din(Din[2]), .We(WE), .Out(Out[2]));
  \锁存器  \u_锁存器_4  (.Din(Din[3]), .We(WE), .Out(Out[3]));
  \锁存器  \u_锁存器_5  (.Din(Din[4]), .We(WE), .Out(Out[4]));
  \锁存器  \u_锁存器_6  (.Din(Din[5]), .We(WE), .Out(Out[5]));
  \锁存器  \u_锁存器_7  (.Din(Din[6]), .We(WE), .Out(Out[6]));
  \锁存器  \u_锁存器_8  (.Din(Din[7]), .We(WE), .Out(Out[7]));
endmodule
