// Digital circuit 驱动器使用案例.dig as structural Verilog
module \驱动器使用案例  (
  input  [7:0] Din,
  input  We,
  input  Oe,
  output [7:0] out_4
);

  wire button_1_out;
  wire [7:0] register_1_q;

  Button button_1 (.out(button_1_out));
  Register #(.Bits(8)) register_1 (.D(Din), .C(button_1_out), .en(We), .Q(register_1_q));
  assign out_4 = Oe ? register_1_q : 8'bz;  // Driver driver_1

  // Notes on the sheet:
  //   驱动器
endmodule
