// Digital circuit 16位的内存.dig as structural Verilog
module \_16位的内存  (
  input  Din,
  input  Str,
  input  Ld,
  input  Row0,
  input  Row1,
  input  Row2,
  input  Row3,
  input  Col0,
  input  Col1,
  input  Col2,
  input  Col3,
  output Out
);

  Memory_Cell memory_cell_1 (.Din(Din), .Str(Str), .Row(Row0), .Column(Col0), .Ld(Ld), .Out(Out));
  Memory_Cell memory_cell_2 (.Din(Din), .Str(Str), .Row(Row1), .Column(Col0), .Ld(Ld), .Out(Out));
  Memory_Cell memory_cell_3 (.Din(Din), .Str(Str), .Row(Row2), .Column(Col0), .Ld(Ld), .Out(Out));
  Memory_Cell memory_cell_4 (.Din(Din), .Str(Str), .Row(Row3), .Column(Col0), .Ld(Ld), .Out(Out));
  Memory_Cell memory_cell_5 (.Din(Din), .Str(Str), .Row(Row0), .Column(Col1), .Ld(Ld), .Out(Out));
  Memory_Cell memory_cell_6 (.Din(Din), .Str(Str), .Row(Row1), .Column(Col1), .Ld(Ld), .Out(Out));
  Memory_Cell memory_cell_7 (.Din(Din), .Str(Str), .Row(Row2), .Column(Col1), .Ld(Ld), .Out(Out));
  Memory_Cell memory_cell_8 (.Din(Din), .Str(Str), .Row(Row3), .Column(Col1), .Ld(Ld), .Out(Out));
  Memory_Cell memory_cell_9 (.Din(Din), .Str(Str), .Row(Row0), .Column(Col2), .Ld(Ld), .Out(Out));
  Memory_Cell memory_cell_10 (.Din(Din), .Str(Str), .Row(Row1), .Column(Col2), .Ld(Ld), .Out(Out));
  Memory_Cell memory_cell_11 (.Din(Din), .Str(Str), .Row(Row2), .Column(Col2), .Ld(Ld), .Out(Out));
  Memory_Cell memory_cell_12 (.Din(Din), .Str(Str), .Row(Row3), .Column(Col2), .Ld(Ld), .Out(Out));
  Memory_Cell memory_cell_13 (.Din(Din), .Str(Str), .Row(Row0), .Column(Col3), .Ld(Ld), .Out(Out));
  Memory_Cell memory_cell_14 (.Din(Din), .Str(Str), .Row(Row1), .Column(Col3), .Ld(Ld), .Out(Out));
  Memory_Cell memory_cell_15 (.Din(Din), .Str(Str), .Row(Row2), .Column(Col3), .Ld(Ld), .Out(Out));
  Memory_Cell memory_cell_16 (.Din(Din), .Str(Str), .Row(Row3), .Column(Col3), .Ld(Ld), .Out(Out));
endmodule
