// Digital circuit 4位寄存器.dig as structural Verilog
module \_4位寄存器  (
  input  [3:0] Din,
  input  clock,
  input  We,
  input  Oe,
  output [3:0] Dout,
  output [3:0] stored_data
);

  Register #(.Bits(4)) register_1 (.D(Din), .C(clock), .en(We), .Q(stored_data));
  assign Dout = Oe ? stored_data : 4'bz;  // Driver driver_1
endmodule
