// Digital circuit 8位数加法器.dig as structural Verilog
module \_8位数加法器  (
  input  A0,
  input  B0,
  input  A1,
  input  B1,
  input  A2,
  input  B2,
  input  A3,
  input  B3,
  input  B4,
  input  B4_2,
  input  A5,
  input  B5,
  input  A6,
  input  B6,
  input  A7,
  input  B7,
  output Sum1,
  output Sum2,
  output Sum3,
  output Sum4,
  output Sum5,
  output Sum6,
  output Sum7,
  output Sum0,
  output Sum8
);

  wire \全加器_1_carry , \全加器_2_carry , \全加器_3_carry , \全加器_4_carry , \全加器_5_carry , \全加器_6_carry ,
       \半加器_1_carry ;

  \半加器  \u_半加器_1  (.A(A0), .B(B0), .Sum(Sum0), .Carry(\半加器_1_carry ));
  \全加器  \u_全加器_1  (.A(A1), .B(B1), .C(\半加器_1_carry ), .Sum(Sum1), .Carry(\全加器_1_carry ));
  \全加器  \u_全加器_2  (.A(A2), .B(B2), .C(\全加器_1_carry ), .Sum(Sum2), .Carry(\全加器_2_carry ));
  \全加器  \u_全加器_3  (.A(A3), .B(B3), .C(\全加器_2_carry ), .Sum(Sum3), .Carry(\全加器_3_carry ));
  \全加器  \u_全加器_4  (.A(B4), .B(B4_2), .C(\全加器_3_carry ), .Sum(Sum4), .Carry(\全加器_4_carry ));
  \全加器  \u_全加器_5  (.A(A5), .B(B5), .C(\全加器_4_carry ), .Sum(Sum5), .Carry(\全加器_5_carry ));
  \全加器  \u_全加器_6  (.A(A6), .B(B6), .C(\全加器_5_carry ), .Sum(Sum6), .Carry(\全加器_6_carry ));
  \全加器  \u_全加器_7  (.A(A7), .B(B7), .C(\全加器_6_carry ), .Sum(Sum7), .Carry(Sum8));
endmodule
