// Digital circuit 8位数加法器1.dig as structural Verilog
module \_8位数加法器1  (
  input  [7:0] A,
  input  [7:0] A_2,
  output Sum8,
  output [7:0] C
);

  wire \全加器_1_carry , \全加器_2_carry , \全加器_3_carry , \全加器_4_carry , \全加器_5_carry , \全加器_6_carry ,
       \半加器_1_carry ;

  \半加器  \u_半加器_1  (.A(A[0]), .B(A_2[0]), .Sum(C[0]), .Carry(\半加器_1_carry ));
  \全加器  \u_全加器_1  (.A(A[1]), .B(A_2[1]), .C(\半加器_1_carry ), .Sum(C[1]), .Carry(\全加器_1_carry ));
  \全加器  \u_全加器_2  (.A(A[2]), .B(A_2[2]), .C(\全加器_1_carry ), .Sum(C[2]), .Carry(\全加器_2_carry ));
  \全加器  \u_全加器_3  (.A(A[3]), .B(A_2[3]), .C(\全加器_2_carry ), .Sum(C[3]), .Carry(\全加器_3_carry ));
  \全加器  \u_全加器_4  (.A(A[4]), .B(A_2[4]), .C(\全加器_3_carry ), .Sum(C[4]), .Carry(\全加器_4_carry ));
  \全加器  \u_全加器_5  (.A(A[5]), .B(A_2[5]), .C(\全加器_4_carry ), .Sum(C[5]), .Carry(\全加器_5_carry ));
  \全加器  \u_全加器_6  (.A(A[6]), .B(A_2[6]), .C(\全加器_5_carry ), .Sum(C[6]), .Carry(\全加器_6_carry ));
  \全加器  \u_全加器_7  (.A(A[7]), .B(A_2[7]), .C(\全加器_6_carry ), .Sum(C[7]), .Carry(Sum8));

  // Notes on the sheet:
  //   A: default 100
  //   A_2: default 100
endmodule
