// Digital circuit 8位数加法器（可控制输出）.dig as structural Verilog
module \_8位数加法器_可控制输出  (
  input  [7:0] RegA,
  input  [7:0] RegB,
  input  Oe,
  output [7:0] Dout,
  output [7:0] ALU_Result,
  output Carry
);

  Add #(.Bits(8)) add_1 (.a(RegA), .b(RegB), .c_i(1'b0), .s(ALU_Result), .c_o(Carry));
  assign Dout = Oe ? ALU_Result : 8'bz;  // Driver driver_1
endmodule
