// Digital circuit Memory_Cell.dig as structural Verilog
module Memory_Cell (
  input  Din,
  input  Str,
  input  Row,
  input  Column,
  input  Ld,
  output Out
);

  wire and_1_out, and_2_out, and_3_out, register_1_q;

  and and_1 (and_1_out, Row, Column);
  and and_2 (and_2_out, Ld, and_1_out);
  and and_3 (and_3_out, Str, and_1_out);
  Register register_1 (.D(Din), .en(and_3_out), .Q(register_1_q));  // open: C
  assign Out = and_2_out ? register_1_q : 1'bz;  // Driver driver_1
endmodule
