// Digital circuit 全加器.dig as structural Verilog
module \全加器  (
  input  A,
  input  B,
  input  C,
  output Sum,
  output Carry
);

  wire \半加器_1_carry , \半加器_1_sum , \半加器_2_carry ;

  \半加器  \u_半加器_1  (.A(A), .B(B), .Sum(\半加器_1_sum ), .Carry(\半加器_1_carry ));
  \半加器  \u_半加器_2  (.A(C), .B(\半加器_1_sum ), .Sum(Sum), .Carry(\半加器_2_carry ));
  \或门制作  \u_或门制作_1  (.B(\半加器_2_carry ), .A(\半加器_1_carry ), .C(Carry));
endmodule
