// Digital circuit 计数器案例.dig as structural Verilog
module \计数器案例  (
  input  EN,
  input  Reset,
  output [1:0] Out,
  output Carry
);

  wire Clock_out;

  Button Clock (.out(Clock_out));
  Counter #(.Bits(2), .isProgramCounter("true")) counter_1 (
    .en(EN), .C(Clock_out), .clr(Reset), .out(Out), .ovf(Carry));
endmodule
