// Digital circuit 输出使能开关案例.dig as structural Verilog
module \输出使能开关案例  (
  input  [1:0] Din,
  input  We,
  input  in_4,
  output Out1,
  output Out2
);

  wire button_1_out;
  wire [1:0] register_1_q;

  Button button_1 (.out(button_1_out));
  Register #(.Bits(2)) register_1 (.D(Din), .C(button_1_out), .en(We), .Q(register_1_q));
  // RelayDT relaydt_1: pin names not known; wires that end beside it: in_4, register_1_q[0], 1'b0, 1'b0, Out1
  // RelayDT relaydt_2: pin names not known; wires that end beside it: in_4, register_1_q[1], Out2
  PullDown pulldown_1 (.out(Out2));
  PullDown pulldown_2 (.out(Out1));
endmodule
