// Digital circuit 锁存器.dig as structural Verilog
module \锁存器  (
  input  Din,
  input  We,
  output Out
);

  wire and_1_out, and_2_out, not_1_out, not_2_out, or_1_out;

  not not_1 (not_1_out, Din);
  and and_1 (and_1_out, Din, We);
  and and_2 (and_2_out, not_1_out, We);
  not not_2 (not_2_out, and_2_out);
  or or_1 (or_1_out, Out, and_1_out);
  and and_3 (Out, or_1_out, not_2_out);
endmodule
